# Fritzing sketch 3w-rgb-led-circuit (saved by Fritzing 0.9.4)
breadboards: 1

parts:
  Part1 = Lithium Ion Cylindrical Battery 3.7v 2200mAh [part_number=1781]  # not connected
  Part2 = Adafruit Feather M0 Express [part_number="Adafruit #3403"]
  Q1 = Basic FET N-Channel [package="DPak [SMD]"]
  Q2 = Basic FET N-Channel [package="DPak [SMD]"]
  Q3 = Basic FET N-Channel [package="DPak [SMD]"]
  3W_RGB_LED1 = 3W RGB LED - Common Anode
  R1 = Resistor [tolerance=±5% resistance=3 package=THT]
  R2 = Resistor [tolerance=±5% resistance=1.75 package=THT]
  R3 = Resistor [tolerance=±5% resistance=1.75 package=THT]

nets:
  N1: Part2.GND, Q1.source, Q2.source, Q3.source
  N2: Part2.VBAT, 3W_RGB_LED1.+
  N3: Part2.D11, Q1.Gate
  N4: Q1.drain, R1.Pin_0
  N5: Q2.drain, R3.Pin_0
  N6: Q3.drain, R2.Pin_0
  N7: 3W_RGB_LED1.G-, R3.Pin_1
  N8: 3W_RGB_LED1.R-, R1.Pin_1
  N9: 3W_RGB_LED1.B-, R2.Pin_1

custom parts:
  Lithium Ion Cylindrical Battery 3.7v 2200mAh: This lithium ion battery has a capacity of 2200mAh and a protection circuit that provides over-voltage, under-voltage and over-current protection. This cell can provide 2C of peak current (4400mA). Note that these batteries are not designed to sustain such high loads, we suggest keeping any constant current draw under about 0.5C (1 Amp).
  Adafruit Feather M0 Express: We love all our Feathers equally, but this Feather is very special. It's our first Feather that is specifically designed for use with CircuitPython! CircuitPython is our beginner-oriented flavor of MicroPython - and as the name hints at, its a small but full-featured version of the popular Python programming language specifically for use with circuitry and electronics. That doesn't mean you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
  3W RGB LED - Common Anode: PCB mounted 3W common anode RGB LED.
